# Fritzing sketch 3.3VAVR_I2CLCD_aitendo (saved by Fritzing 0.9.2b)
breadboards: 2

parts:
  U1 = atmega328 [package=dip]
  U2 = mystery part, 5 pins [chip_label="3.3V Reg"]
  C1 = Ceramic Capacitor [capacitance=100nF package="100 mil [THT, multilayer]"]
  C2 = Ceramic Capacitor [capacitance=100nF package="100 mil [THT, multilayer]"]
  C3 = Ceramic Capacitor [capacitance=100nF package="100 mil [THT, multilayer]"]
  VCC1 = Battery block 9V
  R1 = Resistor [tolerance=±5% resistance=330 package=THT]
  LED1 = LED - 5mm [color="Red (633nm)" package="5 mm [THT]"]
  U3 = mystery part, 9 pins [chip_label=SPLC792]

nets:
  N1: U1.D0_(RX), R1.Pin_1
  N2: U1.VCC, U2.pin3, C1.1, C3.0, U3.pin9
  N3: U1.GND#7, U2.pin1, C1.0, C2.1, C3.1, VCC1.-, LED1.cathode, U3.pin6
  N4: U1.A3, U3.pin3
  N5: U1.A4, U3.pin5
  N6: U1.A5, U3.pin4
  N7: U2.pin5, C2.0, VCC1.+
  N8: R1.Pin_0, LED1.anode
