# Fritzing sketch 5V-3_3V_Regulator (saved by Fritzing 0.9.2b)
breadboards: 1

parts:
  U1 = Voltage Regulator - 5V [package="TO220 [THT]"]
  C1 = Ceramic Capacitor [capacitance=100nF package="100 mil [THT, multilayer]"]
  C2 = Ceramic Capacitor [capacitance=100nF package="100 mil [THT, multilayer]"]
  VCC1 = Battery block 9V
  C3 = Electrolytic Capacitor [capacitance=1µF package="100 mil [THT, electrolytic]"]
  C4 = Electrolytic Capacitor [capacitance=1µF package="100 mil [THT, electrolytic]"]
  U2 = mystery part, 5 pins [chip_label=TL1117-33]
  C5 = Ceramic Capacitor [capacitance=100nF package="100 mil [THT, multilayer]"]
  C6 = Ceramic Capacitor [capacitance=100nF package="100 mil [THT, multilayer]"]
  R1 = Resistor [tolerance=±5% resistance=47 package=THT]
  R2 = Resistor [tolerance=±5% resistance=3.3k package=THT]
  J1 = female pin header, 1 pin [form="♀ (female)"]
  J2 = female pin header, 1 pin [form="♀ (female)"]

nets:
  N1: U1.input_voltage, C1.1, C3.+, U2.pin5, C5.0, R1.Pin_0, J1.pin1
  N2: U1.GND, C1.0, C2.1, VCC1.-, C3.-, C4.-, U2.pin1, C5.1, C6.0, R1.Pin_1, R2.Pin_1
  N3: U1.output_voltage, C2.0, VCC1.+, C4.+
  N4: U2.pin3, C6.1, R2.Pin_0, J2.pin1
