# Fritzing sketch 5VAVR_3.3VI2CLCD-aitendo-NO-Level-Shift-Ext.Crystal_9VPower (saved by Fritzing 0.9.2b)
breadboards: 1

parts:
  U3 = atmega328 [package=dip]
  C1 = Ceramic Capacitor [capacitance=100nF package="100 mil [THT, multilayer]"]
  U4 = mystery part, 5 pins [chip_label=TLV1117-33]
  C2 = Ceramic Capacitor [capacitance=100nF package="100 mil [THT, multilayer]"]
  C3 = Ceramic Capacitor [capacitance=100nF package="100 mil [THT, multilayer]"]
  U1 = mystery part, 9 pins [chip_label=SPLC792-I2C]
  XTAL1 = Crystal [frequency="16 Mhz" package=THT]
  C4 = Ceramic Capacitor [capacitance=100nF package="100 mil [THT, multilayer]"]
  C5 = Ceramic Capacitor [capacitance=100nF package="100 mil [THT, multilayer]"]
  R1 = Resistor [tolerance=±5% resistance=1.2k package=THT]
  R2 = Resistor [tolerance=±5% resistance=2.2k package=THT]
  U5 = Voltage Regulator - Variable [package="TO220 [THT]"]
  C6 = Ceramic Capacitor [capacitance=100nF package="100 mil [THT, multilayer]"]
  C7 = Ceramic Capacitor [capacitance=100nF package="100 mil [THT, multilayer]"]
  C8 = Electrolytic Capacitor [capacitance=1µF package="100 mil [THT, electrolytic]"]
  C9 = Electrolytic Capacitor [capacitance=1µF package="100 mil [THT, electrolytic]"]
  VCC1 = Battery block 9V
  C10 = Electrolytic Capacitor [capacitance=1µF package="100 mil [THT, electrolytic]"]

nets:
  N1: U3.VCC, C1.0, U4.pin5, C3.0, U5.ADJ, C6.1, C8.+
  N2: U3.GND#7, C1.1, U4.pin1, C2.0, C3.1, U1.pin6, C4.0, C5.1, R2.Pin_1, U5.OUT, C6.0, C7.1, C8.-, C9.-, VCC1.-, C10.-
  N3: U3.XLAT1, XTAL1.pin_0, C4.1
  N4: U3.XLAT2, XTAL1.pin_1, C5.0
  N5: U3.A3, R1.Pin_0
  N6: U3.A4, U1.pin5
  N7: U3.A5, U1.pin4
  N8: U4.pin3, C2.1, U1.pin9, C10.+
  N9: U1.pin3, R1.Pin_1, R2.Pin_0
  N10: U5.IN, C7.0, C9.+, VCC1.+

notes:
  GND
  3.3V
  GND
  5V
