# Fritzing sketch 5VAVR_3.3VI2CLCD-aitendo (saved by Fritzing 0.9.2b)
breadboards: 1

parts:
  U2 = mystery part, 8 pins [chip_label=PCA9306]
  U3 = atmega328 [package=dip]
  C1 = Ceramic Capacitor [capacitance=100nF package="100 mil [THT, multilayer]"]
  U4 = mystery part, 5 pins [chip_label=TLV1117-33]
  C2 = Ceramic Capacitor [capacitance=100nF package="100 mil [THT, multilayer]"]
  C3 = Ceramic Capacitor [capacitance=100nF package="100 mil [THT, multilayer]"]
  U1 = mystery part, 9 pins [chip_label=SPLC792-I2C]
  VCC1 = 4 x AAA Battery Mount  # not connected

nets:
  N1: U2.pin1, U4.pin3, C2.1, U1.pin3, U1.pin9
  N2: U2.pin2, U1.pin4
  N3: U2.pin3, U1.pin5
  N4: U2.pin5, U3.GND#7, C1.1, U4.pin1, C2.0, C3.1, U1.pin6
  N5: U2.pin6, U3.A4
  N6: U2.pin7, U3.A5
  N7: U2.pin8, U3.VCC, C1.0, U4.pin5, C3.0

notes:
  GND
  3.3V
  GND
  5V
  RC 8MHz
  5V電源
