# Fritzing sketch 5VAVR_3.3VI2CLCD (saved by Fritzing 0.9.2b)
breadboards: 1

parts:
  U1 = mystery part, 5 pins [chip_label=AQM0802]
  U2 = mystery part, 8 pins [chip_label=PCA9306]
  U3 = atmega328 [package=dip]
  C1 = Ceramic Capacitor [capacitance=100nF package="100 mil [THT, multilayer]"]
  U4 = mystery part, 5 pins [chip_label=TLV1117-33]
  C2 = Ceramic Capacitor [capacitance=100nF package="100 mil [THT, multilayer]"]
  C3 = Ceramic Capacitor [capacitance=100nF package="100 mil [THT, multilayer]"]
  R1 = Resistor [tolerance=±5% resistance=220 package=THT]
  LED1 = LED - 5mm [color="Red (633nm)" package="5 mm [THT]"]

nets:
  N1: U1.pin1, U1.pin2, U2.pin1, U4.pin3, C2.1
  N2: U1.pin3, U2.pin2
  N3: U1.pin4, U2.pin3
  N4: U1.pin5, U2.pin5, U3.GND#7, C1.1, U4.pin1, C2.0, C3.1, LED1.cathode
  N5: U2.pin6, U3.A4
  N6: U2.pin7, U3.A5
  N7: U2.pin8, U3.VCC, C1.0, U4.pin5, C3.0
  N8: U3.D0_(RX), R1.Pin_0
  N9: R1.Pin_1, LED1.anode

notes:
  GND
  3.3V
  GND
  5V
  1MHz
