# Fritzing sketch ATMega328P_16MHz (saved by Fritzing 0.9.2b)
breadboards: 1

parts:
  U1 = atmega328 [package=dip]
  XTAL1 = Crystal [frequency="16 Mhz" package=THT]
  C1 = Ceramic Capacitor [capacitance=100nF package="100 mil [THT, multilayer]"]
  C2 = Ceramic Capacitor [capacitance=100nF package="100 mil [THT, multilayer]"]
  U2 = mystery part, 6 pins [chip_label="AVR Programmer"]
  R1 = Resistor [tolerance=±5% resistance=330 package=THT]
  LED1 = LED - 5mm [color="Red (633nm)" package="5 mm [THT]"]

nets:
  N1: U1.RESET, U2.pin3
  N2: U1.D0_(RX), R1.Pin_1
  N3: U1.VCC, U2.pin1
  N4: U1.GND#7, C1.1, C2.0, U2.pin2, LED1.cathode
  N5: U1.XLAT1, XTAL1.pin_0, C2.1
  N6: U1.XLAT2, XTAL1.pin_1, C1.0
  N7: U1.D11_(PWM), U2.pin6
  N8: U1.D12, U2.pin5
  N9: U1.D13, U2.pin4
  N10: R1.Pin_0, LED1.anode
