# Fritzing sketch MOS-FET_Switching_Test (saved by Fritzing 0.9.2b)
breadboards: 1

parts:
  U1 = atmega328 [package=dip]
  C1 = Ceramic Capacitor [capacitance=100nF package="100 mil [THT, multilayer]"]
  RE1 = Rotary Encoder [package=THT]
  S1 = Pushbutton [package=THT]
  R1 = Resistor [tolerance=±5% resistance=1k package=THT]
  R2 = Resistor [tolerance=±5% resistance=1k package=THT]
  LED1 = LED - 5mm [color="Red (633nm)" package="5 mm [THT]"]
  LED2 = LED - 5mm [color="Green (570nm)" package="5 mm [THT]"]
  XTAL1 = Crystal [frequency="16 Mhz" package=THT]
  C2 = Ceramic Capacitor [capacitance=100nF package="100 mil [THT, multilayer]"]
  C3 = Ceramic Capacitor [capacitance=100nF package="100 mil [THT, multilayer]"]
  Q1 = NPN-Transistor [package="TO92 [THT]"]
  Q2 = NPN-Transistor [package="TO92 [THT]"]
  Q3 = Basic FET N-Channel [package="TO220 [THT]"]
  LED3 = LED - 5mm [color="Blue (525nm)" package="5 mm [THT]"]
  R3 = Resistor [tolerance=±5% resistance=1k package=THT]

nets:
  N1: U1.D0_(RX), RE1.EncoderPinA
  N2: U1.D1_(TX), RE1.EncoderPinB
  N3: U1.D2, S1.leg1
  N4: U1.VCC, C1.0, R1.Pin_0, R2.Pin_0, R3.Pin_0
  N5: U1.GND#7, C1.1, RE1.EncoderPinC, S1.leg0, C2.1, C3.0, Q1.E, Q2.E, Q3.source
  N6: U1.XLAT1, XTAL1.pin_0, C3.1
  N7: U1.XLAT2, XTAL1.pin_1, C2.0
  N8: U1.D11_(PWM), Q2.B
  N9: U1.D12, Q1.B
  N10: U1.D13, Q3.gate
  N11: R1.Pin_1, LED2.anode
  N12: R2.Pin_1, LED1.anode
  N13: LED1.cathode, Q2.C
  N14: LED2.cathode, Q1.C
  N15: Q3.drain, LED3.cathode
  N16: LED3.anode, R3.Pin_1
