# Fritzing sketch POT_accuracy (saved by Fritzing 0.9.2b)

parts:
  パーツ1 = Arduino Uno (Rev3)
  R1 = Rotary Potentiometer (Small) [maximum_resistance=100kΩ package=THT]

nets:
  N1: パーツ1.A0, R1.wiper
  N2: パーツ1.5V, R1.leg2
  N3: パーツ1.GND, R1.leg1
