# Fritzing sketch SQR_FG_ケース内配線_Ver.2 (saved by Fritzing 0.9.2b)
perfboards: 2

parts:
  J1 = female pin header, 3 pins [form="♀ (female)"]
  J2 = female pin header, 4 pins [form="♀ (female)"]
  J3 = female pin header, 4 pins [form="♀ (female)"]
  RE1 = Rotary Encoder [package=THT]
  S1 = Pushbutton [package=THT]
  R1 = Rotary Potentiometer (Small) [maximum_resistance=100kΩ package=THT]
  VCC1 = Battery block 9V
  S2 = Toggle Switch [package=THT]
  R2 = Rotary Potentiometer (Small) [maximum_resistance=100kΩ package=THT]
  TRS1 = Audio Jack (TRS) 3.5mm [package="4Ucon 08780 [THT]"]
  J4 = female pin header, 5 pins [form="♀ (female)"]
  S3 = Toggle Switch [package=THT]
  J6 = female pin header, 2 pins [form="♀ (female)"]
  J9 = female pin header, 3 pins [form="♀ (female)"]

nets:
  N1: J1.pin1, R1.leg1
  N2: J1.pin2, R1.wiper
  N3: J1.pin3, R1.leg2
  N4: J2.pin1, RE1.EncoderPinB
  N5: J2.pin2, RE1.EncoderPinC
  N6: J2.pin3, S1.leg0
  N7: J2.pin4, RE1.EncoderPinA, S1.leg1
  N8: J3.pin2, R2.leg1
  N9: VCC1.-, J4.pin2
  N10: S2.COM, J4.pin1
  N11: R2.wiper, TRS1.Tip
  N12: R2.leg2, TRS1.Sleeve, S3.COM
  N13: J4.pin4, J9.pin2
  N14: J4.pin5, J9.pin1
  N15: S3.L1, J6.pin2

notes:
  +9V
  GND
  NC
  GND
  +5V
  Rotary Encoder
  w/ Switch
  Duty POT
  OC1A
  WAVE_OUT
  NC
  NC
  Level
  1 GND
  2 Wave_Out
  3 Wave_In
  GND
  GND_OUT
  VCC/2
  OutPut
  T:Wave
  S:GND
  デジタル基板
  出力基板
  Ver.2
