# Fritzing sketch SQR_OUT (saved by Fritzing 0.9.2b)
breadboards: 2
perfboards: 1

parts:
  U1 = atmega328 [package=dip]
  C1 = Ceramic Capacitor [capacitance=100nF package="100 mil [THT, multilayer]"]
  XTAL1 = Crystal [frequency="16 Mhz" package=THT]
  C2 = Ceramic Capacitor [capacitance=22nF package="100 mil [THT, multilayer]"]
  C3 = Ceramic Capacitor [capacitance=22pF package="100 mil [THT, multilayer]"]
  R1 = Rotary Potentiometer (Small) [maximum_resistance=100kΩ package=THT]
  R2 = Rotary Potentiometer (Small) [maximum_resistance=100kΩ package=THT]
  IC1 = Dual Op-Amp [package=dip08]
  R3 = Rotary Potentiometer (Small) [maximum_resistance=100kΩ package=THT]
  R4 = Resistor [tolerance=±5% resistance=220 package=THT]
  J1 = female pin header, 1 pin [form="♀ (female)"]
  J2 = female pin header, 1 pin [form="♀ (female)"]
  RE1 = Rotary Encoder [package=THT]
  S1 = Pushbutton [package=THT]
  R5 = Resistor [tolerance=±5% resistance=220 package=THT]
  C4 = Electrolytic Capacitor [capacitance=47µF package="100 mil [THT, electrolytic]"]
  C5 = Electrolytic Capacitor [capacitance=47µF package="100 mil [THT, electrolytic]"]

nets:
  N1: U1.D2, S1.leg1
  N2: U1.D3_(PWM), RE1.EncoderPinB
  N3: U1.D4, RE1.EncoderPinC
  N4: U1.VCC, U1.AREF, C1.0, R1.leg1, R2.leg1, IC1.A_V+, R5.Pin_0, C4.+
  N5: U1.GND#7, C1.1, C2.1, C3.1, R1.leg2, R2.leg2, IC1.A_V-, R3.leg1, R4.Pin_1, RE1.EncoderPinA, S1.leg0, C5.-
  N6: U1.XLAT1, XTAL1.pin_0, C3.0
  N7: U1.XLAT2, XTAL1.pin_1, C2.0
  N8: U1.D9_(PWM), R3.leg2
  N9: U1.A0, R2.wiper
  N10: U1.A1, R1.wiper
  N11: IC1.A_OUT, IC1.A_-IN, J1.pin1
  N12: IC1.A_+IN, R4.Pin_0, R5.Pin_1, C4.-, C5.+
  N13: IC1.B_+IN, R3.wiper
  N14: IC1.B_-IN, IC1.B_OUT, J2.pin1

notes:
  Freq
  Adj
  VGND
  OUT
  Vol
  Rotary
  Encoder
