# Fritzing sketch SQ_FG_Simple_Output_Test (saved by Fritzing 0.9.2b)
breadboards: 1
perfboards: 1

parts:
  R1 = Resistor [tolerance=±5% resistance=1k package=THT]
  R2 = Resistor [tolerance=±5% resistance=1k package=THT]
  VCC1 = Battery
  J1 = female pin header, 3 pins [form="♀ (female)"]
  J2 = female pin header, 2 pins [form="♀ (female)"]

nets:
  N1: R1.Pin_0, J2.pin2
  N2: R1.Pin_1, R2.Pin_0
  N3: VCC1.+, J1.pin1
  N4: J1.pin2, J1.pin3

notes:
  GND
  VCC
  GND
  VCC/2
  TLE2426
  Board
