# Fritzing sketch VGND_and_Compaletor (saved by Fritzing 0.9.2b)
breadboards: 2

parts:
  IC1 = Dual Op-Amp [package=dip08]
  IC2 = Dual Op-Amp [package=dip08]
  R1 = Resistor [tolerance=±5% resistance=10k package=THT]
  R2 = Resistor [tolerance=±5% resistance=10k package=THT]
  C1 = Electrolytic Capacitor [capacitance=1µF package="100 mil [THT, electrolytic]"]
  C2 = Electrolytic Capacitor [capacitance=1µF package="100 mil [THT, electrolytic]"]
  J2 = female pin header, 1 pin [form="♀ (female)"]
  U2 = atmega328 [package=dip]
  LED1 = LED - 5mm [color="Red (633nm)" package="5 mm [THT]"]
  LED2 = LED - 5mm [color="Blue (525nm)" package="5 mm [THT]"]
  R3 = Resistor [tolerance=±5% resistance=1k package=THT]
  R4 = Resistor [tolerance=±5% resistance=330 package=THT]  # not connected
  XTAL1 = Crystal [frequency="16 Mhz" package=THT]
  C3 = Ceramic Capacitor [capacitance=100nF package="100 mil [THT, multilayer]"]
  C4 = Ceramic Capacitor [capacitance=100nF package="100 mil [THT, multilayer]"]
  C5 = Ceramic Capacitor [capacitance=100nF package="100 mil [THT, multilayer]"]
  C6 = Ceramic Capacitor [capacitance=100nF package="100 mil [THT, multilayer]"]
  R5 = Resistor [tolerance=±5% resistance=1k package=THT]

nets:
  N1: IC1.A_V-, IC2.A_V-, R2.Pin_1, C2.-, U2.GND#7, R3.Pin_0, C3.1, C4.1, C5.1, C6.0
  N2: IC1.B_+IN, U2.D10_(PWM), LED2.anode
  N3: IC1.B_-IN, IC2.B_-IN, IC2.B_OUT, R5.Pin_0
  N4: IC1.B_OUT, J2.pin1, R5.Pin_1
  N5: IC1.A_V+, IC2.A_V+, R1.Pin_0, C1.+, U2.VCC, U2.AREF, C3.0, C6.1
  N6: IC2.B_+IN, R1.Pin_1, R2.Pin_0, C1.-, C2.+
  N7: U2.XLAT1, XTAL1.pin_0, C5.0
  N8: U2.XLAT2, XTAL1.pin_1, C4.0
  N9: U2.D9_(PWM), LED1.anode
  N10: LED1.cathode, R3.Pin_1

notes:
  VGND
  VCC
  VEE
  NC
  VEE
  VCC
